// Digital circuit ALU.dig as structural Verilog
module ALU (
  input  [7:0] A,
  input  [7:0] B,
  input  [2:0] Sel,
  output [7:0] S
);

  wire adderr_8bits_1_c0, sub_1_c_o;
  wire [7:0] ADD, AND, demultiplexer_1_out_0, demultiplexer_1_out_1, demultiplexer_1_out_2,
       demultiplexer_1_out_3, demultiplexer_1_out_4, demultiplexer_1_out_5, demultiplexer_1_out_6,
       demultiplexer_1_out_7, demultiplexer_2_out_0, demultiplexer_2_out_1, demultiplexer_2_out_2,
       demultiplexer_2_out_3, demultiplexer_2_out_4, demultiplexer_2_out_5, demultiplexer_2_out_6,
       demultiplexer_2_out_7, DIV, div_1_r, MUL, NEG, NOT, OR, SUB;
  wire [15:8] mul_1_mul;

  Multiplexer #(.Selector_Bits(3), .Bits(8)) multiplexer_1 (
    .sel(Sel), .in_0(ADD), .in_1(SUB), .in_2(MUL), .in_3(DIV), .in_4(AND), .in_5(OR), .in_6(NOT), .in_7(NEG),
    .out(S));
  Demultiplexer #(.Selector_Bits(3), .Bits(8)) demultiplexer_1 (
    .sel(Sel), .in(A), .out_0(demultiplexer_1_out_0), .out_1(demultiplexer_1_out_1),
    .out_2(demultiplexer_1_out_2), .out_3(demultiplexer_1_out_3), .out_4(demultiplexer_1_out_4),
    .out_5(demultiplexer_1_out_5), .out_6(demultiplexer_1_out_6), .out_7(demultiplexer_1_out_7));
  Demultiplexer #(.Bits(8), .Selector_Bits(3)) demultiplexer_2 (
    .sel(Sel), .in(B), .out_0(demultiplexer_2_out_0), .out_1(demultiplexer_2_out_1),
    .out_2(demultiplexer_2_out_2), .out_3(demultiplexer_2_out_3), .out_4(demultiplexer_2_out_4),
    .out_5(demultiplexer_2_out_5), .out_6(demultiplexer_2_out_6), .out_7(demultiplexer_2_out_7));
  Neg #(.Bits(8)) neg_1 (.in(demultiplexer_1_out_7), .out(NEG));
  assign NOT = ~demultiplexer_1_out_6;  // Not not_1, 8 bits wide
  assign AND = demultiplexer_1_out_4 & demultiplexer_2_out_4;  // And and_1, 8 bits wide
  assign OR = demultiplexer_1_out_5 | demultiplexer_2_out_5;  // Or or_1, 8 bits wide
  Adderr_8bits adderr_8bits_1 (
    .A(demultiplexer_1_out_0), .Ci(1'b0), .B(demultiplexer_2_out_0), .S7(ADD[6]), .S6(ADD[5]), .S5(ADD[4]),
    .S4(ADD[3]), .S3(ADD[2]), .S2(ADD[1]), .S1(ADD[0]), .S8(ADD[7]), .C0(adderr_8bits_1_c0));
  Sub #(.Bits(8)) sub_1 (.a(demultiplexer_1_out_1), .b(demultiplexer_2_out_1), .c_i(1'b0), .s(SUB), .c_o(sub_1_c_o));
  Mul #(.Bits(8)) mul_1 (.a(demultiplexer_1_out_2), .b(demultiplexer_2_out_2), .mul({mul_1_mul, MUL}));
  Div #(.Bits(8)) div_1 (.a(demultiplexer_1_out_3), .b(demultiplexer_2_out_3), .q(DIV), .r(div_1_r));
endmodule
