// Digital circuit Adderr_8bits.dig as structural Verilog
module Adderr_8bits (
  input  [7:0] A,
  input  Ci,
  input  [7:0] B,
  output S7,
  output S6,
  output S5,
  output S4,
  output S3,
  output S2,
  output S1,
  output S8,
  output C0
);

  wire bussplitter_1_d0, bussplitter_1_d1, bussplitter_1_d2, bussplitter_1_d3, bussplitter_1_d4,
       bussplitter_1_d5, bussplitter_1_d6, bussplitter_1_d7, bussplitter_2_d0, bussplitter_2_d1,
       bussplitter_2_d2, bussplitter_2_d3, bussplitter_2_d4, bussplitter_2_d5, bussplitter_2_d6,
       bussplitter_2_d7, fadder_1__1st_bit, fadder_1__2nd_bit, fadder_2__1st_bit, fadder_2__2nd_bit,
       fadder_3__1st_bit, fadder_3__2nd_bit, fadder_4__1st_bit, fadder_4__2nd_bit, fadder_5__1st_bit,
       fadder_5__2nd_bit, fadder_6__1st_bit, fadder_6__2nd_bit, fadder_7__1st_bit, fadder_7__2nd_bit,
       fadder_8__1st_bit, fadder_8__2nd_bit, fadder_9__2nd_bit, fadder_10__1st_bit, fadder_10__2nd_bit,
       fadder_11__1st_bit, fadder_11__2nd_bit, fadder_12__1st_bit, fadder_12__2nd_bit, fadder_13__1st_bit,
       fadder_13__2nd_bit, fadder_14__1st_bit, fadder_14__2nd_bit, fadder_15__1st_bit, fadder_15__2nd_bit,
       fadder_16__1st_bit, fadder_16__2nd_bit, fadder_17__2nd_bit, fadder_18__1st_bit, fadder_18__2nd_bit,
       fadder_19__1st_bit, fadder_19__2nd_bit, fadder_20__1st_bit, fadder_20__2nd_bit, fadder_21__1st_bit,
       fadder_21__2nd_bit, fadder_22__1st_bit, fadder_22__2nd_bit, fadder_23__1st_bit, fadder_23__2nd_bit,
       fadder_24__1st_bit, fadder_25__2nd_bit, fadder_26__1st_bit, fadder_26__2nd_bit, fadder_27__1st_bit,
       fadder_27__2nd_bit, fadder_28__1st_bit, fadder_28__2nd_bit, fadder_29__1st_bit, fadder_29__2nd_bit,
       fadder_30__1st_bit, fadder_30__2nd_bit, fadder_31__1st_bit, fadder_32__1st_bit, fadder_32__2nd_bit,
       fadder_33__1st_bit, fadder_33__2nd_bit, fadder_34__1st_bit, fadder_34__2nd_bit, fadder_35__1st_bit,
       fadder_36__2nd_bit, fadder_37__1st_bit, fadder_37__2nd_bit, fadder_38__2nd_bit, fadder_39__1st_bit,
       fadder_39__2nd_bit, fadder_40__1st_bit, fadder_40__2nd_bit, fadder_41__1st_bit, fadder_41__2nd_bit,
       fadder_42__1st_bit, fadder_43__2nd_bit, fadder_44__1st_bit, fadder_44__2nd_bit, fadder_45__1st_bit,
       fadder_45__2nd_bit, fadder_46__1st_bit, fadder_47__2nd_bit, fadder_48__1st_bit, fadder_48__2nd_bit,
       fadder_49__1st_bit, fadder_50__2nd_bit, fadder_51__1st_bit;

  BusSplitter #(.Bits(8)) bussplitter_1 (
    .D(A), .OE(1'b1), .D0(bussplitter_1_d0), .D1(bussplitter_1_d1), .D2(bussplitter_1_d2),
    .D3(bussplitter_1_d3), .D4(bussplitter_1_d4), .D5(bussplitter_1_d5), .D6(bussplitter_1_d6),
    .D7(bussplitter_1_d7));
  FAdder fadder_1 (.A(Ci), .B(bussplitter_1_d0), ._2nd_bit(fadder_1__2nd_bit), ._1st_bit(fadder_1__1st_bit));
  FAdder fadder_2 (
    .A(fadder_1__2nd_bit), .B(bussplitter_1_d1), ._2nd_bit(fadder_2__2nd_bit), ._1st_bit(fadder_2__1st_bit));
  FAdder fadder_3 (
    .A(fadder_2__2nd_bit), .B(bussplitter_1_d2), ._2nd_bit(fadder_3__2nd_bit), ._1st_bit(fadder_3__1st_bit));
  FAdder fadder_4 (
    .A(fadder_3__2nd_bit), .B(bussplitter_1_d3), ._2nd_bit(fadder_4__2nd_bit), ._1st_bit(fadder_4__1st_bit));
  FAdder fadder_5 (
    .A(fadder_4__2nd_bit), .B(bussplitter_1_d4), ._2nd_bit(fadder_5__2nd_bit), ._1st_bit(fadder_5__1st_bit));
  FAdder fadder_6 (
    .A(fadder_5__2nd_bit), .B(bussplitter_1_d5), ._2nd_bit(fadder_6__2nd_bit), ._1st_bit(fadder_6__1st_bit));
  FAdder fadder_7 (
    .A(fadder_6__2nd_bit), .B(bussplitter_1_d6), ._2nd_bit(fadder_7__2nd_bit), ._1st_bit(fadder_7__1st_bit));
  FAdder fadder_8 (
    .A(fadder_7__2nd_bit), .B(bussplitter_1_d7), ._2nd_bit(fadder_8__2nd_bit), ._1st_bit(fadder_8__1st_bit));
  BusSplitter #(.Bits(8)) bussplitter_2 (
    .D(B), .OE(1'b1), .D0(bussplitter_2_d0), .D1(bussplitter_2_d1), .D2(bussplitter_2_d2),
    .D3(bussplitter_2_d3), .D4(bussplitter_2_d4), .D5(bussplitter_2_d5), .D6(bussplitter_2_d6),
    .D7(bussplitter_2_d7));
  FAdder fadder_9 (.A(bussplitter_2_d0), .B(fadder_1__1st_bit), ._2nd_bit(fadder_9__2nd_bit), ._1st_bit(S1));
  FAdder fadder_10 (
    .A(bussplitter_2_d1), .B(fadder_2__1st_bit), ._2nd_bit(fadder_10__2nd_bit), ._1st_bit(fadder_10__1st_bit));
  FAdder fadder_11 (
    .A(bussplitter_2_d2), .B(fadder_3__1st_bit), ._2nd_bit(fadder_11__2nd_bit), ._1st_bit(fadder_11__1st_bit));
  FAdder fadder_12 (
    .A(bussplitter_2_d3), .B(fadder_4__1st_bit), ._2nd_bit(fadder_12__2nd_bit), ._1st_bit(fadder_12__1st_bit));
  FAdder fadder_13 (
    .A(bussplitter_2_d4), .B(fadder_5__1st_bit), ._2nd_bit(fadder_13__2nd_bit), ._1st_bit(fadder_13__1st_bit));
  FAdder fadder_14 (
    .A(bussplitter_2_d5), .B(fadder_6__1st_bit), ._2nd_bit(fadder_14__2nd_bit), ._1st_bit(fadder_14__1st_bit));
  FAdder fadder_15 (
    .A(bussplitter_2_d6), .B(fadder_7__1st_bit), ._2nd_bit(fadder_15__2nd_bit), ._1st_bit(fadder_15__1st_bit));
  FAdder fadder_16 (
    .A(bussplitter_2_d7), .B(fadder_8__1st_bit), ._2nd_bit(fadder_16__2nd_bit), ._1st_bit(fadder_16__1st_bit));
  FAdder fadder_17 (.A(fadder_9__2nd_bit), .B(fadder_10__1st_bit), ._2nd_bit(fadder_17__2nd_bit), ._1st_bit(S2));
  FAdder fadder_18 (
    .A(fadder_11__2nd_bit), .B(fadder_12__1st_bit), ._2nd_bit(fadder_18__2nd_bit),
    ._1st_bit(fadder_18__1st_bit));
  FAdder fadder_19 (
    .A(fadder_13__2nd_bit), .B(fadder_14__1st_bit), ._2nd_bit(fadder_19__2nd_bit),
    ._1st_bit(fadder_19__1st_bit));
  FAdder fadder_20 (
    .A(fadder_15__2nd_bit), .B(fadder_16__1st_bit), ._2nd_bit(fadder_20__2nd_bit),
    ._1st_bit(fadder_20__1st_bit));
  FAdder fadder_21 (
    .A(fadder_10__2nd_bit), .B(fadder_11__1st_bit), ._2nd_bit(fadder_21__2nd_bit),
    ._1st_bit(fadder_21__1st_bit));
  FAdder fadder_22 (
    .A(fadder_12__2nd_bit), .B(fadder_13__1st_bit), ._2nd_bit(fadder_22__2nd_bit),
    ._1st_bit(fadder_22__1st_bit));
  FAdder fadder_23 (
    .A(fadder_14__2nd_bit), .B(fadder_15__1st_bit), ._2nd_bit(fadder_23__2nd_bit),
    ._1st_bit(fadder_23__1st_bit));
  FAdder fadder_24 (.A(fadder_16__2nd_bit), .B(fadder_8__2nd_bit), ._1st_bit(fadder_24__1st_bit));  // open: _2nd_bit
  FAdder fadder_25 (.A(fadder_17__2nd_bit), .B(fadder_21__1st_bit), ._2nd_bit(fadder_25__2nd_bit), ._1st_bit(S3));
  FAdder fadder_26 (
    .A(fadder_21__2nd_bit), .B(fadder_18__1st_bit), ._2nd_bit(fadder_26__2nd_bit),
    ._1st_bit(fadder_26__1st_bit));
  FAdder fadder_27 (
    .A(fadder_18__2nd_bit), .B(fadder_22__1st_bit), ._2nd_bit(fadder_27__2nd_bit),
    ._1st_bit(fadder_27__1st_bit));
  FAdder fadder_28 (
    .A(fadder_22__2nd_bit), .B(fadder_19__1st_bit), ._2nd_bit(fadder_28__2nd_bit),
    ._1st_bit(fadder_28__1st_bit));
  FAdder fadder_29 (
    .A(fadder_19__2nd_bit), .B(fadder_23__1st_bit), ._2nd_bit(fadder_29__2nd_bit),
    ._1st_bit(fadder_29__1st_bit));
  FAdder fadder_30 (
    .A(fadder_23__2nd_bit), .B(fadder_20__1st_bit), ._2nd_bit(fadder_30__2nd_bit),
    ._1st_bit(fadder_30__1st_bit));
  FAdder fadder_31 (.A(fadder_20__2nd_bit), .B(fadder_24__1st_bit), ._1st_bit(fadder_31__1st_bit));  // open: _2nd_bit
  FAdder fadder_32 (
    .A(fadder_26__2nd_bit), .B(fadder_27__1st_bit), ._2nd_bit(fadder_32__2nd_bit),
    ._1st_bit(fadder_32__1st_bit));
  FAdder fadder_33 (
    .A(fadder_27__2nd_bit), .B(fadder_28__1st_bit), ._2nd_bit(fadder_33__2nd_bit),
    ._1st_bit(fadder_33__1st_bit));
  FAdder fadder_34 (
    .A(fadder_29__2nd_bit), .B(fadder_30__1st_bit), ._2nd_bit(fadder_34__2nd_bit),
    ._1st_bit(fadder_34__1st_bit));
  FAdder fadder_35 (.A(fadder_30__2nd_bit), .B(fadder_31__1st_bit), ._1st_bit(fadder_35__1st_bit));  // open: _2nd_bit
  FAdder fadder_36 (.A(fadder_25__2nd_bit), .B(fadder_26__1st_bit), ._2nd_bit(fadder_36__2nd_bit), ._1st_bit(S4));
  FAdder fadder_37 (
    .A(fadder_28__2nd_bit), .B(fadder_29__1st_bit), ._2nd_bit(fadder_37__2nd_bit),
    ._1st_bit(fadder_37__1st_bit));
  FAdder fadder_38 (.A(fadder_36__2nd_bit), .B(fadder_32__1st_bit), ._2nd_bit(fadder_38__2nd_bit), ._1st_bit(S5));
  FAdder fadder_39 (
    .A(fadder_32__2nd_bit), .B(fadder_33__1st_bit), ._2nd_bit(fadder_39__2nd_bit),
    ._1st_bit(fadder_39__1st_bit));
  FAdder fadder_40 (
    .A(fadder_33__2nd_bit), .B(fadder_37__1st_bit), ._2nd_bit(fadder_40__2nd_bit),
    ._1st_bit(fadder_40__1st_bit));
  FAdder fadder_41 (
    .A(fadder_37__2nd_bit), .B(fadder_34__1st_bit), ._2nd_bit(fadder_41__2nd_bit),
    ._1st_bit(fadder_41__1st_bit));
  FAdder fadder_42 (.A(fadder_34__2nd_bit), .B(fadder_35__1st_bit), ._1st_bit(fadder_42__1st_bit));  // open: _2nd_bit
  FAdder fadder_43 (.A(fadder_38__2nd_bit), .B(fadder_39__1st_bit), ._2nd_bit(fadder_43__2nd_bit), ._1st_bit(S6));
  FAdder fadder_44 (
    .A(fadder_39__2nd_bit), .B(fadder_40__1st_bit), ._2nd_bit(fadder_44__2nd_bit),
    ._1st_bit(fadder_44__1st_bit));
  FAdder fadder_45 (
    .A(fadder_40__2nd_bit), .B(fadder_41__1st_bit), ._2nd_bit(fadder_45__2nd_bit),
    ._1st_bit(fadder_45__1st_bit));
  FAdder fadder_46 (.A(fadder_41__2nd_bit), .B(fadder_42__1st_bit), ._1st_bit(fadder_46__1st_bit));  // open: _2nd_bit
  FAdder fadder_47 (.A(fadder_43__2nd_bit), .B(fadder_44__1st_bit), ._2nd_bit(fadder_47__2nd_bit), ._1st_bit(S7));
  FAdder fadder_48 (
    .A(fadder_44__2nd_bit), .B(fadder_45__1st_bit), ._2nd_bit(fadder_48__2nd_bit),
    ._1st_bit(fadder_48__1st_bit));
  FAdder fadder_49 (.A(fadder_45__2nd_bit), .B(fadder_46__1st_bit), ._1st_bit(fadder_49__1st_bit));  // open: _2nd_bit
  FAdder fadder_50 (.A(fadder_47__2nd_bit), .B(fadder_48__1st_bit), ._2nd_bit(fadder_50__2nd_bit), ._1st_bit(S8));
  FAdder fadder_51 (.A(fadder_48__2nd_bit), .B(fadder_49__1st_bit), ._1st_bit(fadder_51__1st_bit));  // open: _2nd_bit
  FAdder fadder_52 (.A(fadder_50__2nd_bit), .B(fadder_51__1st_bit), ._1st_bit(C0));  // open: _2nd_bit
endmodule
