// Digital circuit CLOCK SELECT.dig as structural Verilog
module CLOCK_SELECT (
  input  Clk,
  input  [1:0] K,
  output M,
  output R
);

  wire and_1_out, and_2_out, and_4_out, and_5_out, not_1_out, not_2_out;

  and and_1 (and_1_out, Clk, K[0]);
  and and_2 (and_2_out, Clk, K[1]);
  not not_1 (not_1_out, and_1_out);
  not not_2 (not_2_out, and_2_out);
  and and_3 (M, Clk, not_1_out, and_2_out);
  and and_4 (and_4_out, and_1_out, Clk);
  and and_5 (and_5_out, not_2_out, Clk);
  or or_1 (R, and_4_out, and_5_out);
endmodule
