// Digital circuit DFlipFlop.dig as structural Verilog
module DFlipFlop (
  input  D,
  input  EN,
  output C0
);

  wire and_1_out, and_2_out, and_3_out, and_4_out, nor_1_out, nor_2_out, nor_4_out, not_1_out, not_2_out,
       not_3_out;

  not not_1 (not_1_out, D);
  and and_1 (and_1_out, not_1_out, EN);
  and and_2 (and_2_out, EN, D);
  nor nor_1 (nor_1_out, and_1_out, nor_2_out);
  nor nor_2 (nor_2_out, nor_1_out, and_2_out);
  not not_2 (not_2_out, EN);
  not not_3 (not_3_out, nor_1_out);
  and and_3 (and_3_out, not_3_out, not_2_out);
  and and_4 (and_4_out, not_2_out, nor_1_out);
  nor nor_3 (C0, and_3_out, nor_4_out);
  nor nor_4 (nor_4_out, C0, and_4_out);
endmodule
