// Digital circuit FAdder.dig as structural Verilog
module FAdder (
  input  A,
  input  B,
  output _2nd_bit,
  output _1st_bit
);

  wire not_1_out, or_1_out;

  HAdder hadder_1 (.Entry_A(A), .Entry_B(B), .Output(_2nd_bit));
  or or_1 (or_1_out, A, B);
  not not_1 (not_1_out, _2nd_bit);
  and and_1 (_1st_bit, not_1_out, or_1_out);
endmodule
