// Digital circuit RAM2bit.dig as structural Verilog
module RAM2bit (
  input  [7:0] Data,
  input  Clk,
  input  [1:0] L,
  input  [1:0] C,
  input  R___W,
  output [7:0] S
);

  wire and_1_out, and_2_out, and_3_out, and_4_out, demultiplexer_2_out_0, demultiplexer_2_out_1,
       demultiplexer_2_out_2, demultiplexer_2_out_3, demultiplexer_3_out_0, demultiplexer_3_out_1,
       demultiplexer_3_out_2, demultiplexer_3_out_3, demultiplexer_4_out_0, demultiplexer_4_out_1,
       demultiplexer_4_out_2, demultiplexer_4_out_3, demultiplexer_5_out_0, demultiplexer_5_out_1,
       demultiplexer_5_out_2, demultiplexer_5_out_3;
  wire [1:0] demultiplexer_1_out_0, demultiplexer_1_out_1, demultiplexer_1_out_2, demultiplexer_1_out_3;
  wire [7:0] multiplexer_1_out, multiplexer_2_out, multiplexer_3_out, multiplexer_4_out, multiplexer_5_out,
       word8bit_1_s, word8bit_2_s, word8bit_3_s, word8bit_4_s, word8bit_5_s, word8bit_6_s, word8bit_7_s,
       word8bit_8_s, word8bit_9_s, word8bit_10_s, word8bit_11_s, word8bit_12_s, word8bit_13_s, word8bit_14_s,
       word8bit_15_s, word8bit_16_s;

  Demultiplexer #(.Bits(2), .Selector_Bits(2)) demultiplexer_1 (
    .sel(L), .in(C), .out_0(demultiplexer_1_out_0), .out_1(demultiplexer_1_out_1),
    .out_2(demultiplexer_1_out_2), .out_3(demultiplexer_1_out_3));
  WORD8bit word8bit_1 (.Data(Data), .R___W(demultiplexer_2_out_3), .Clk(Clk), .S(word8bit_1_s));
  WORD8bit word8bit_2 (.Data(Data), .R___W(demultiplexer_3_out_3), .Clk(Clk), .S(word8bit_2_s));
  WORD8bit word8bit_3 (.Data(Data), .R___W(demultiplexer_4_out_3), .Clk(Clk), .S(word8bit_3_s));
  WORD8bit word8bit_4 (.Data(Data), .R___W(demultiplexer_5_out_3), .Clk(Clk), .S(word8bit_4_s));
  WORD8bit word8bit_5 (.Data(Data), .R___W(demultiplexer_2_out_2), .Clk(Clk), .S(word8bit_5_s));
  WORD8bit word8bit_6 (.Data(Data), .R___W(demultiplexer_3_out_2), .Clk(Clk), .S(word8bit_6_s));
  WORD8bit word8bit_7 (.Data(Data), .R___W(demultiplexer_4_out_2), .Clk(Clk), .S(word8bit_7_s));
  WORD8bit word8bit_8 (.Data(Data), .R___W(demultiplexer_5_out_2), .Clk(Clk), .S(word8bit_8_s));
  Demultiplexer #(.Selector_Bits(2)) demultiplexer_2 (
    .sel(demultiplexer_1_out_0), .in(and_1_out), .out_0(demultiplexer_2_out_0),
    .out_1(demultiplexer_2_out_1), .out_2(demultiplexer_2_out_2), .out_3(demultiplexer_2_out_3));
  WORD8bit word8bit_9 (.Data(Data), .R___W(demultiplexer_2_out_1), .Clk(Clk), .S(word8bit_9_s));
  Demultiplexer #(.Selector_Bits(2)) demultiplexer_3 (
    .sel(demultiplexer_1_out_1), .in(and_2_out), .out_0(demultiplexer_3_out_0),
    .out_1(demultiplexer_3_out_1), .out_2(demultiplexer_3_out_2), .out_3(demultiplexer_3_out_3));
  WORD8bit word8bit_10 (.Data(Data), .R___W(demultiplexer_3_out_1), .Clk(Clk), .S(word8bit_10_s));
  Demultiplexer #(.Selector_Bits(2)) demultiplexer_4 (
    .sel(demultiplexer_1_out_2), .in(and_3_out), .out_0(demultiplexer_4_out_0),
    .out_1(demultiplexer_4_out_1), .out_2(demultiplexer_4_out_2), .out_3(demultiplexer_4_out_3));
  WORD8bit word8bit_11 (.Data(Data), .R___W(demultiplexer_4_out_1), .Clk(Clk), .S(word8bit_11_s));
  Demultiplexer #(.Selector_Bits(2)) demultiplexer_5 (
    .sel(demultiplexer_1_out_3), .in(and_4_out), .out_0(demultiplexer_5_out_0),
    .out_1(demultiplexer_5_out_1), .out_2(demultiplexer_5_out_2), .out_3(demultiplexer_5_out_3));
  WORD8bit word8bit_12 (.Data(Data), .R___W(demultiplexer_5_out_1), .Clk(Clk), .S(word8bit_12_s));
  and and_1 (and_1_out, R___W, 1'b1);
  and and_2 (and_2_out, R___W, 1'b1);
  and and_3 (and_3_out, R___W, 1'b1);
  and and_4 (and_4_out, R___W, 1'b1);
  WORD8bit word8bit_13 (.Data(Data), .R___W(demultiplexer_2_out_0), .Clk(Clk), .S(word8bit_13_s));
  WORD8bit word8bit_14 (.Data(Data), .R___W(demultiplexer_3_out_0), .Clk(Clk), .S(word8bit_14_s));
  WORD8bit word8bit_15 (.Data(Data), .R___W(demultiplexer_4_out_0), .Clk(Clk), .S(word8bit_15_s));
  WORD8bit word8bit_16 (.Data(Data), .R___W(demultiplexer_5_out_0), .Clk(Clk), .S(word8bit_16_s));
  Multiplexer #(.Bits(8), .Selector_Bits(2)) multiplexer_1 (
    .sel(demultiplexer_1_out_0), .in_0(word8bit_13_s), .in_1(word8bit_9_s), .in_2(word8bit_5_s),
    .in_3(word8bit_1_s), .out(multiplexer_1_out));
  Multiplexer #(.Selector_Bits(2), .Bits(8)) multiplexer_2 (
    .sel(demultiplexer_1_out_1), .in_0(word8bit_14_s), .in_1(word8bit_10_s), .in_2(word8bit_6_s),
    .in_3(word8bit_2_s), .out(multiplexer_2_out));
  Multiplexer #(.Selector_Bits(2), .Bits(8)) multiplexer_3 (
    .sel(demultiplexer_1_out_2), .in_0(word8bit_15_s), .in_1(word8bit_11_s), .in_2(word8bit_7_s),
    .in_3(word8bit_3_s), .out(multiplexer_3_out));
  Multiplexer #(.Selector_Bits(2), .Bits(8)) multiplexer_4 (
    .sel(demultiplexer_1_out_3), .in_0(word8bit_16_s), .in_1(word8bit_12_s), .in_2(word8bit_8_s),
    .in_3(word8bit_4_s), .out(multiplexer_4_out));
  Multiplexer #(.Bits(8), .Selector_Bits(2)) multiplexer_5 (
    .sel(C), .in_0(multiplexer_1_out), .in_1(multiplexer_2_out), .in_2(multiplexer_3_out),
    .in_3(multiplexer_4_out), .out(multiplexer_5_out));
  Multiplexer #(.Bits(8)) multiplexer_6 (.sel(R___W), .in_0(multiplexer_5_out), .in_1({8{1'b0}}), .out(S));

  // Other names for the same wires on the sheet: RW = R___W
endmodule
