// Digital circuit REG4BITSDECAL.dig as structural Verilog
module REG4BITSDECAL (
  input  Clk,
  input  Is,
  input  Load,
  input  [3:0] Ip,
  output Os,
  output [3:0] Op
);

  wire multiplexer_1_out, multiplexer_2_out, multiplexer_3_out, multiplexer_4_out;

  Multiplexer multiplexer_1 (.sel(Load), .in_0(Is), .in_1(Ip[3]), .out(multiplexer_1_out));
  DLatch dlatch_1 (.D(multiplexer_1_out), .EN(Clk), .C0(Op[3]));
  Multiplexer multiplexer_2 (.sel(Load), .in_0(Op[3]), .in_1(Ip[2]), .out(multiplexer_2_out));
  DLatch dlatch_2 (.D(multiplexer_2_out), .EN(Clk), .C0(Op[2]));
  Multiplexer multiplexer_3 (.sel(Load), .in_0(Op[2]), .in_1(Ip[1]), .out(multiplexer_3_out));
  DLatch dlatch_3 (.D(multiplexer_3_out), .EN(Clk), .C0(Op[1]));
  Multiplexer multiplexer_4 (.sel(Load), .in_0(Op[1]), .in_1(Ip[0]), .out(multiplexer_4_out));
  DLatch dlatch_4 (.D(multiplexer_4_out), .EN(Clk), .C0(Op[0]));

  assign Os = Op[0];
endmodule
