// Digital circuit REG8BITS.dig as structural Verilog
module REG8BITS (
  input  Clk,
  input  Load,
  input  [7:0] Ip,
  output [7:0] Os
);

  REG4BITSDECAL reg4bitsdecal_1 (.Clk(Clk), .Is(1'b0), .Load(Load), .Ip(Ip[3:0]), .Op(Os[3:0]));  // open: Os
  REG4BITSDECAL reg4bitsdecal_2 (.Clk(Clk), .Is(1'b0), .Load(Load), .Ip(Ip[7:4]), .Op(Os[7:4]));  // open: Os

  // Other names for the same wires on the sheet: Ip1[3:0] = Ip[3:0]; Ip2[3:0] = Ip[7:4]
endmodule
