// Digital circuit REGISTERS.dig as structural Verilog
module REGISTERS (
  input  [7:0] I,
  input  [1:0] Sel,
  input  Clk,
  output [7:0] R0,
  output [7:0] R1,
  output [7:0] R2,
  output [7:0] R3
);

  wire and_1_out, and_2_out, and_3_out, and_4_out, demultiplexer_2_out_0, demultiplexer_2_out_1,
       demultiplexer_2_out_2, demultiplexer_2_out_3;
  wire [7:0] demultiplexer_1_out_0, demultiplexer_1_out_1, demultiplexer_1_out_2, demultiplexer_1_out_3;

  Demultiplexer #(.Selector_Bits(2), .Bits(8)) demultiplexer_1 (
    .sel(Sel), .in(I), .out_0(demultiplexer_1_out_0), .out_1(demultiplexer_1_out_1),
    .out_2(demultiplexer_1_out_2), .out_3(demultiplexer_1_out_3));
  Demultiplexer #(.Selector_Bits(2)) demultiplexer_2 (
    .sel(Sel), .in(1'b1), .out_0(demultiplexer_2_out_0), .out_1(demultiplexer_2_out_1),
    .out_2(demultiplexer_2_out_2), .out_3(demultiplexer_2_out_3));
  and and_1 (and_1_out, Clk, demultiplexer_2_out_0);
  and and_2 (and_2_out, Clk, demultiplexer_2_out_1);
  and and_3 (and_3_out, Clk, demultiplexer_2_out_2);
  and and_4 (and_4_out, Clk, demultiplexer_2_out_3);
  REG8BITS reg8bits_1 (.Clk(and_1_out), .Load(demultiplexer_2_out_0), .Ip(demultiplexer_1_out_0), .Os(R0));
  REG8BITS reg8bits_2 (.Clk(and_2_out), .Load(demultiplexer_2_out_1), .Ip(demultiplexer_1_out_1), .Os(R1));
  REG8BITS reg8bits_3 (.Clk(and_3_out), .Load(demultiplexer_2_out_2), .Ip(demultiplexer_1_out_2), .Os(R2));
  REG8BITS reg8bits_4 (.Clk(and_4_out), .Load(demultiplexer_2_out_3), .Ip(demultiplexer_1_out_3), .Os(R3));
endmodule
