// Digital circuit REG_SELECT.dig as structural Verilog
module REG_SELECT (
  input  [7:0] R0,
  input  [7:0] R1,
  input  [7:0] R3,
  input  [7:0] R2,
  input  [1:0] Sel,
  output [7:0] S
);

  Multiplexer #(.Bits(8), .Selector_Bits(2)) multiplexer_1 (
    .sel(Sel), .in_0(R0), .in_1(R1), .in_2(R2), .in_3(R3), .out(S));
endmodule
