// Digital circuit Reg_8bits.dig as structural Verilog
module Reg_8bits (
  input  [7:0] I,
  input  W,
  output [7:0] O
);

  DLatch dlatch_1 (.D(I[7]), .EN(W), .C0(O[7]));
  DLatch dlatch_2 (.D(I[6]), .EN(W), .C0(O[6]));
  DLatch dlatch_3 (.D(I[5]), .EN(W), .C0(O[5]));
  DLatch dlatch_4 (.D(I[4]), .EN(W), .C0(O[4]));
  DLatch dlatch_5 (.D(I[3]), .EN(W), .C0(O[3]));
  DLatch dlatch_6 (.D(I[2]), .EN(W), .C0(O[2]));
  DLatch dlatch_7 (.D(I[1]), .EN(W), .C0(O[1]));
  DLatch dlatch_8 (.D(I[0]), .EN(W), .C0(O[0]));
endmodule
