// Digital circuit TP1 EX1 - EX3.dig as structural Verilog
module TP1_EX1___EX3 (
  input  in_1,
  input  in_3,
  input  in_4,
  input  in_6,
  input  in_7,
  input  in_9,
  input  in_10,
  input  in_11,
  input  in_12,
  output out_2,
  output out_5,
  output out_8,
  output out_13
);

  wire and_1_out, fgnfet_1_s, or_1_out;

  FGNFET fgnfet_1 (.G(in_4), .D(out_5), .S(fgnfet_1_s));
  NFET nfet_1 (.G(in_3), .D(fgnfet_1_s), .S(1'b0));
  and and_1 (and_1_out, in_10, in_9);
  PullUp pullup_1 (.out(out_2));
  NFET nfet_2 (.G(in_1), .D(out_2), .S(1'b0));
  PullUp pullup_2 (.out(out_5));
  or or_1 (or_1_out, in_11, and_1_out);
  NFET nfet_3 (.G(in_7), .D(out_8), .S(1'b0));
  or or_2 (out_13, or_1_out, in_12);
  PullUp pullup_3 (.out(out_8));
  NFET nfet_4 (.G(in_6), .D(1'b0), .S(out_8));
endmodule
