// Digital circuit UDC.dig as structural Verilog
module UDC (
  input  [1:0] K,
  input  [2:0] O,
  input  [1:0] Ra,
  input  [1:0] Rb,
  input  [7:0] Imm,
  input  [1:0] R,
  input  clk,
  input  [7:0] Min,
  output [7:0] Cm,
  output [7:0] Mout
);

  wire clock_select_1_m, clock_select_1_r;
  wire [7:0] alu_1_s, driver_1_out, reg_select_1_s, reg_select_2_s, registers_1_r0, registers_1_r1,
       registers_1_r2, registers_1_r3;

  REGISTERS registers_1 (
    .I(driver_1_out), .Sel(R), .Clk(clk), .R0(registers_1_r0), .R1(registers_1_r1), .R2(registers_1_r2),
    .R3(registers_1_r3));
  assign driver_1_out = clock_select_1_r ? alu_1_s : 8'bz;  // Driver driver_1
  CLOCK_SELECT clock_select_1 (.Clk(clk), .K(K), .M(clock_select_1_m), .R(clock_select_1_r));
  REG_SELECT reg_select_1 (
    .R0(registers_1_r0), .R1(registers_1_r1), .R3(registers_1_r3), .R2(registers_1_r2), .Sel(Ra),
    .S(reg_select_1_s));
  REG_SELECT reg_select_2 (
    .R0(registers_1_r0), .R1(registers_1_r1), .R3(registers_1_r3), .R2(registers_1_r2), .Sel(Rb),
    .S(reg_select_2_s));
  ALU alu_1 (.A(reg_select_1_s), .B(reg_select_2_s), .Sel(O), .S(alu_1_s));
  assign Mout = clock_select_1_m ? Min : 8'bz;  // Driver driver_2
  assign Cm = clock_select_1_m ? alu_1_s : 8'bz;  // Driver driver_3
endmodule
