// Digital circuit WORD8bit.dig as structural Verilog
module WORD8bit (
  input  [7:0] Data,
  input  R___W,
  input  Clk,
  output [7:0] S
);

  wire and_1_out;
  wire [7:0] reg8bits_1_os;

  and and_1 (and_1_out, R___W, Clk);
  REG8BITS reg8bits_1 (.Clk(and_1_out), .Load(R___W), .Ip(Data), .Os(reg8bits_1_os));
  Multiplexer #(.Bits(8)) multiplexer_1 (.sel(R___W), .in_0(reg8bits_1_os), .in_1({8{1'b0}}), .out(S));
endmodule
