// Digital circuit arith.dig as structural Verilog
module arith (
  input  [7:0] A,
  input  [7:0] B,
  input  Selector,
  output S1,
  output S2,
  output S3,
  output S4,
  output S5,
  output S6,
  output S7,
  output S8,
  output C0
);

  wire ST1, ST2, ST3, ST4, ST5, ST6, ST7, ST8, sub_1_c_o, sub_1_s, sub_2_c_o, sub_2_s, sub_3_c_o, sub_3_s,
       sub_4_c_o, sub_4_s, sub_5_c_o, sub_5_s, sub_6_c_o, sub_6_s, sub_7_c_o, sub_7_s, sub_8_s;
  wire [7:0] demultiplexer_1_out_0, demultiplexer_1_out_1, demultiplexer_2_out_0, demultiplexer_2_out_1;

  Demultiplexer #(.Bits(8)) demultiplexer_1 (
    .sel(Selector), .in(A), .out_0(demultiplexer_1_out_0), .out_1(demultiplexer_1_out_1));
  Demultiplexer #(.Bits(8)) demultiplexer_2 (
    .sel(Selector), .in(B), .out_0(demultiplexer_2_out_0), .out_1(demultiplexer_2_out_1));
  Adderr_8bits adderr_8bits_1 (
    .A(demultiplexer_1_out_0), .Ci(1'b0), .B(demultiplexer_2_out_0), .S7(ST7), .S6(ST6), .S5(ST5), .S4(ST4),
    .S3(ST3), .S2(ST2), .S1(ST1), .S8(ST8), .C0(C0));
  Sub sub_1 (.a(demultiplexer_1_out_1[0]), .b(demultiplexer_2_out_1[0]), .c_i(1'b0), .s(sub_1_s), .c_o(sub_1_c_o));
  Sub sub_2 (.a(demultiplexer_1_out_1[1]), .b(demultiplexer_2_out_1[1]), .c_i(sub_1_c_o), .s(sub_2_s), .c_o(sub_2_c_o));
  Sub sub_3 (.a(demultiplexer_1_out_1[2]), .b(demultiplexer_2_out_1[2]), .c_i(sub_2_c_o), .s(sub_3_s), .c_o(sub_3_c_o));
  Sub sub_4 (.a(demultiplexer_1_out_1[3]), .b(demultiplexer_2_out_1[3]), .c_i(sub_3_c_o), .s(sub_4_s), .c_o(sub_4_c_o));
  Sub sub_5 (.a(demultiplexer_1_out_1[4]), .b(demultiplexer_2_out_1[4]), .c_i(sub_4_c_o), .s(sub_5_s), .c_o(sub_5_c_o));
  Sub sub_6 (.a(demultiplexer_1_out_1[5]), .b(demultiplexer_2_out_1[5]), .c_i(sub_5_c_o), .s(sub_6_s), .c_o(sub_6_c_o));
  Sub sub_7 (.a(demultiplexer_1_out_1[6]), .b(demultiplexer_2_out_1[6]), .c_i(sub_6_c_o), .s(sub_7_s), .c_o(sub_7_c_o));
  Sub sub_8 (.a(demultiplexer_1_out_1[7]), .b(demultiplexer_2_out_1[7]), .c_i(sub_7_c_o), .s(sub_8_s));  // open: c_o
  or or_1 (S1, ST1, sub_1_s);
  or or_2 (S2, ST2, sub_2_s);
  or or_3 (S3, ST3, sub_3_s);
  or or_4 (S4, ST4, sub_4_s);
  or or_5 (S5, ST5, sub_5_s);
  or or_6 (S6, ST6, sub_6_s);
  or or_7 (S7, ST7, sub_7_s);
  or or_8 (S8, ST8, sub_8_s);

  // Other names for the same wires on the sheet: ST9 = C0

  // Notes on the sheet:
  //   Selector: 0 = add
  //   1 = minus
  //   ADD
  //   SUB
endmodule
