// Digital circuit ual.dig as structural Verilog
module ual (
  input  [7:0] A,
  input  [7:0] B,
  input  [2:0] S,
  output C0,
  output [7:0] O
);

  wire and_2_out, not_1_out, not_2_out, not_3_out;
  wire [7:0] and1, and2, andF, ariF, demultiplexer_1_out_0, demultiplexer_1_out_4, demultiplexer_1_out_5,
       demultiplexer_1_out_6, demultiplexer_1_out_7, demultiplexer_2_out_0, demultiplexer_2_out_4,
       demultiplexer_2_out_5, demultiplexer_2_out_6, demultiplexer_2_out_7, not_4_out, or1, or2, sbF;

  and and_1 (sbF[0], S[0], not_1_out, S[2]);
  not not_1 (not_1_out, S[1]);
  and and_2 (and_2_out, S[0], not_3_out, not_2_out);
  not not_2 (not_2_out, S[2]);
  not not_3 (not_3_out, S[1]);
  Demultiplexer #(.Bits(8), .Selector_Bits(3)) demultiplexer_1 (
    .sel(S), .in(A), .out_0(demultiplexer_1_out_0), .out_1(demultiplexer_1_out_0), .out_2(and1), .out_3(or1),
    .out_4(demultiplexer_1_out_4), .out_5(demultiplexer_1_out_5), .out_6(demultiplexer_1_out_6),
    .out_7(demultiplexer_1_out_7));
  Demultiplexer #(.Selector_Bits(3), .Bits(8)) demultiplexer_2 (
    .sel(S), .in(B), .out_0(demultiplexer_2_out_0), .out_1(demultiplexer_2_out_0), .out_2(and2), .out_3(or2),
    .out_4(demultiplexer_2_out_4), .out_5(demultiplexer_2_out_5), .out_6(demultiplexer_2_out_6),
    .out_7(demultiplexer_2_out_7));
  arith arith_1 (
    .A(demultiplexer_1_out_0), .B(demultiplexer_2_out_0), .Selector(and_2_out), .S1(ariF[0]), .S2(ariF[1]),
    .S3(ariF[2]), .S4(ariF[3]), .S5(ariF[4]), .S6(ariF[5]), .S7(ariF[6]), .S8(ariF[7]), .C0(C0));
  assign not_4_out = ~demultiplexer_1_out_7;  // Not not_4, 8 bits wide
  Multiplexer #(.Bits(8), .Selector_Bits(3)) multiplexer_1 (
    .sel(S), .in_0(ariF), .in_1(ariF), .in_2(andF), .in_3(andF), .in_4(sbF), .in_5(sbF),
    .in_6(demultiplexer_1_out_6), .in_7(not_4_out), .out(O));
  and and_3 (andF[0], and1[0], and2[0]);
  and and_4 (andF[1], and1[1], and2[1]);
  and and_5 (andF[2], and1[2], and2[2]);
  and and_6 (andF[3], and1[3], and2[3]);
  and and_7 (andF[4], and1[4], and2[4]);
  and and_8 (andF[5], and1[5], and2[5]);
  and and_9 (andF[6], and1[6], and2[6]);
  and and_10 (andF[7], and1[7], and2[7]);
  or or_1 (andF[0], or1[0], or2[0]);
  or or_2 (andF[1], or1[1], or2[1]);
  or or_3 (andF[2], or1[2], or2[2]);
  or or_4 (andF[3], or1[3], or2[3]);
  or or_5 (andF[4], or1[4], or2[4]);
  or or_6 (andF[5], or1[5], or2[5]);
  or or_7 (andF[6], or1[6], or2[6]);
  or or_8 (andF[7], or1[7], or2[7]);
  // Pins of 1 and 8 bits meet at sbF

  // Notes on the sheet:
  //   Sub
  //   AND
  //   OR
endmodule
